# Fritzing sketch weather (saved by Fritzing 0.9.4)
circuit board: 5.2cm x 3.6cm
breadboards: 1

parts:
  C2 = Ceramic Capacitor [capacitance="100 nF" package="1206 [SMD, multilayer]"]
  S1_RESET = Pushbutton [package="[THT]"]
  S2_MODE = Pushbutton [package="[THT]"]
  R1 = Resistor [tolerance=±5% resistance=10k package=THT]
  R2 = Resistor [tolerance=±5% resistance=10k package=THT]
  R3 = Resistor [tolerance=±5% resistance=220k package=THT]
  R4 = Resistor [tolerance=±5% resistance=68k package=THT]
  Li-ion_4_2V = Battery
  R5 = Resistor [tolerance=±5% resistance=10k package=THT]
  R6 = Resistor [tolerance=±5% resistance=10k package=THT]
  R7 = Resistor [tolerance=±5% resistance=10k package=THT]
  R8 = Resistor [tolerance=±5% resistance=10k package=THT]
  U2 = MPC1700 [package=sot23-3]
  R9 = Resistor [tolerance=±5% resistance=10k package=THT]
  DHT1 = DHT11 Humitidy and Temperature Sensor
  ESP-12F = Gizwits WiFi Witty ESP-12F
  C1 = Electrolytic Capacitor [capacitance=1000µF voltage=20V package="200 mil [THT, electrolytic]"]

nets:
  GND: C2.0, S1_RESET.Pin_1, S1_RESET.Pin_2, R1.Pin_1, R4.Pin_1, Li-ion_4_2V.-, R8.Pin_1, U2.GND, DHT1.GND, ESP-12F.GND, C1.-
  3.3V: C2.1, S2_MODE.Pin_3, S2_MODE.Pin_4, R2.Pin_0, R5.Pin_0, R6.Pin_1, R7.Pin_1, U2.OUT, R9.Pin_1, DHT1.VDD, ESP-12F.VCC, C1.+
  GPIO16/REST: S1_RESET.Pin_3, S1_RESET.Pin_4, R2.Pin_1, ESP-12F.REST, ESP-12F.GPIO16
  GPIO14: S2_MODE.Pin_1, S2_MODE.Pin_2, R1.Pin_0, ESP-12F.GPIO14
  N1: R3.Pin_0, Li-ion_4_2V.+, U2.IN
  vccm: R3.Pin_1, R4.Pin_0, ESP-12F.ADC
  N2: R5.Pin_1, ESP-12F.CH_PD
  GPIO0: R6.Pin_0, ESP-12F.GPIO0
  GPIO2: R7.Pin_0, ESP-12F.GPIO2
  N3: R8.Pin_0, ESP-12F.GPIO15
  GPIO4: R9.Pin_0, DHT1.DATA, ESP-12F.GPIO4

notes:
  Reset & Wakeup
  Mode selection
  Power supply

custom parts:
  MPC1700: Small package LDO
  DHT11 Humitidy and Temperature Sensor: DHT11 Humidity and Temperature Sensor
